// Logisim project Tucano-8.circ as structural Verilog: 17 circuits, main circuit Registers
module Registers (
  input  [7:0] WriteData,
  input  WE,
  input  RegWrite,
  input  [1:0] rd,
  input  [1:0] rs,
  input  [1:0] rW,
  input  CLK,
  input  RST,
  output [7:0] rd_out,
  output [7:0] rs_out
);

  wire and_1_out, demultiplexer_1_out0, demultiplexer_1_out1, demultiplexer_1_out2, demultiplexer_1_out3;
  wire [7:0] r0_q, r1_q, r2_q, r3_q;

  and and_1 (and_1_out, WE, RegWrite);
  Demultiplexer #(.select(2)) demultiplexer_1 (
    .out0(demultiplexer_1_out0), .out1(demultiplexer_1_out1), .out2(demultiplexer_1_out2),
    .out3(demultiplexer_1_out3), .in(and_1_out), .sel(rW));
  Register r0 (.D(WriteData), .en(demultiplexer_1_out0), .clk(CLK), .Q(r0_q), .clr(RST));
  Register r1 (.D(WriteData), .en(demultiplexer_1_out1), .clk(CLK), .Q(r1_q), .clr(RST));
  Register r2 (.D(WriteData), .en(demultiplexer_1_out2), .clk(CLK), .Q(r2_q), .clr(RST));
  Register r3 (.D(WriteData), .en(demultiplexer_1_out3), .clk(CLK), .Q(r3_q), .clr(RST));
  Multiplexer #(.select(2), .width(8)) multiplexer_1 (
    .in0(r0_q), .in1(r1_q), .in2(r2_q), .in3(r3_q), .out(rd_out), .sel(rd));
  Multiplexer #(.select(2), .width(8)) multiplexer_2 (
    .in0(r0_q), .in1(r1_q), .in2(r2_q), .in3(r3_q), .out(rs_out), .sel(rs));
endmodule

module ALU (
  input  [7:0] RD,
  input  [7:0] RS,
  input  [3:0] ALUOp,
  output [7:0] C,
  output Zero
);

  wire comparator_1_eq, comparator_1_gt, comparator_1_lt;
  wire [7:0] adder_1_out, and_1_out, bit_extender_1_out, multiplexer_1_out, multiplexer_2_out, not_1_out,
       or_1_out, shifter_1_out, shifter_2_out, subtractor_1_out;

  Adder adder_1 (.a(RD), .b(RS), .out(adder_1_out));  // open: cin, cout
  Subtractor subtractor_1 (.a(RD), .b(RS), .out(subtractor_1_out));  // open: bin, bout
  assign and_1_out = RD & RS;  // AND_Gate and_1, 8 bits wide
  assign or_1_out = RD | RS;  // OR_Gate or_1, 8 bits wide
  assign not_1_out = ~RD;  // NOT_Gate not_1, 8 bits wide
  Shifter shifter_1 (.in(RD), .\dist (3'b001), .out(shifter_1_out));
  Shifter #(.shift("lr")) shifter_2 (.in(RD), .\dist (3'b001), .out(shifter_2_out));
  Comparator comparator_1 (.a(RD), .b(RS), .gt(comparator_1_gt), .eq(comparator_1_eq), .lt(comparator_1_lt));
  assign bit_extender_1_out = {{7{comparator_1_lt}}, comparator_1_lt};  // Bit_Extender bit_extender_1
  Multiplexer #(.width(8)) multiplexer_1 (.in1(8'h1), .out(multiplexer_1_out), .sel(comparator_1_gt));  // open: in0
  Multiplexer #(.width(8)) multiplexer_2 (
    .in1({8{1'b1}}), .out(multiplexer_2_out), .sel(comparator_1_eq));  // open: in0
  Multiplexer #(.select(4), .width(8)) multiplexer_3 (
    .in0(adder_1_out), .in1(subtractor_1_out), .in2(and_1_out), .in3(or_1_out), .in4(not_1_out),
    .in5(shifter_1_out), .in6(shifter_2_out), .in7(multiplexer_1_out), .in8(bit_extender_1_out),
    .in9(multiplexer_2_out), .in13({4'b0000, RS[3:0]}), .out(C), .sel(ALUOp));  // open: in10, in11, in12, in14, in15
  Comparator comparator_2 (.a(C), .b({8{1'b0}}), .eq(Zero));  // open: gt, lt
endmodule

module UC (
  input  [3:0] Opcode,
  output Jump,
  output MemRead,
  output MemWrite,
  output MemToReg,
  output RegDstLogic,
  output ALUSrc,
  output Branch,
  output [3:0] ALUOp,
  output RegWrite
);

  jumpUC jumpuc_1 (.n4(Opcode[0]), .n5(Opcode[1]), .n6(Opcode[2]), .n7(Opcode[3]), .Jump(Jump));
  MemReadUC memreaduc_1 (.n4(Opcode[0]), .n5(Opcode[1]), .n6(Opcode[2]), .n7(Opcode[3]), .MemRead(MemRead));
  MemWriteUC memwriteuc_1 (.n4(Opcode[0]), .n5(Opcode[1]), .n6(Opcode[2]), .n7(Opcode[3]), .MemWrite(MemWrite));
  MemToRegUC memtoreguc_1 (.n4(Opcode[0]), .n5(Opcode[1]), .n6(Opcode[2]), .n7(Opcode[3]), .MemToReg(MemToReg));
  RegDstUC regdstuc_1 (
    .n4(Opcode[0]), .n5(Opcode[1]), .n6(Opcode[2]), .n7(Opcode[3]), .RegDstLogic(RegDstLogic));  // open: in_5, in_6, in_7, in_8
  ALUSrcUC alusrcuc_1 (.n4(Opcode[0]), .n5(Opcode[1]), .n6(Opcode[2]), .n7(Opcode[3]), .ALUSrc(ALUSrc));
  BranchUC branchuc_1 (.n4(Opcode[0]), .n5(Opcode[1]), .n6(Opcode[2]), .n7(Opcode[3]), .Branch(Branch));
  ALUopUC aluopuc_1 (.n4(Opcode[0]), .n5(Opcode[1]), .n6(Opcode[2]), .n7(Opcode[3]), .ALUOp(ALUOp));
  RegWriteUC regwriteuc_1 (.n4(Opcode[0]), .n5(Opcode[1]), .n6(Opcode[2]), .n7(Opcode[3]), .RegWrite(RegWrite));
endmodule

module RAM_8b (
  input  [7:0] A,
  input  MemWrite,
  input  MemRead,
  input  [7:0] Din,
  input  CLK,
  output [7:0] Dout
);

  wire [7:0] ram_1_data;

  RAM #(.databus("bidir")) ram_1 (.addr(A), .we(MemWrite), .oe(MemRead), .clk(CLK), .data(ram_1_data));
  Demultiplexer #(.width(8)) demultiplexer_1 (.out1(Dout), .in(ram_1_data), .sel(MemRead));  // open: out0
  Multiplexer #(.width(8)) multiplexer_1 (.in1(Din), .out(ram_1_data), .sel(MemWrite));  // open: in0
endmodule

module ROM_8b (
  input  [7:0] PC,
  output [7:0] RD,
  output [7:0] RS,
  output [7:0] Op
);

  // ROM #(.dataWidth(24), .line("dual")) rom_1: pin names not known; wires that end beside it: PC
endmodule

module jumpUC (
  input  n4,
  input  n5,
  input  n6,
  input  n7,
  output Jump
);

  wire not_1_out, not_2_out;

  not not_1 (not_1_out, n4);
  not not_2 (not_2_out, n6);
  and and_1 (Jump, not_1_out, n5, not_2_out, n7);
endmodule

module MemReadUC (
  input  n4,
  input  n5,
  input  n6,
  input  n7,
  output MemRead
);

  wire not_1_out;

  not not_1 (not_1_out, n4);
  and and_1 (MemRead, not_1_out, n5, n6, n7);
endmodule

module MemWriteUC (
  input  n4,
  input  n5,
  input  n6,
  input  n7,
  output MemWrite
);

  and STH (MemWrite, n4, n5, n6, n7);
endmodule

module RegWriteUC (
  input  n4,
  input  n5,
  input  n6,
  input  n7,
  output RegWrite
);

  wire add_out, E_out, EQU_out, GTH_out, MV_out, NO_out, not_1_out, not_2_out, not_3_out, not_4_out,
       not_5_out, not_6_out, not_7_out, not_8_out, not_9_out, not_10_out, not_11_out, not_12_out, not_13_out,
       not_14_out, not_15_out, not_16_out, not_17_out, not_18_out, not_19_out, not_20_out, not_21_out,
       not_22_out, not_23_out, not_24_out, not_25_out, not_26_out, OU_out, READ_out, SHL_out, SHR_out,
       sub_out;

  not not_1 (not_1_out, n4);
  not not_2 (not_2_out, n5);
  and add (add_out, not_1_out, not_2_out, not_3_out, not_4_out);
  not not_3 (not_3_out, n6);
  not not_4 (not_4_out, n7);
  not not_5 (not_5_out, n5);
  and sub (sub_out, n4, not_5_out, not_6_out, not_7_out);
  not not_6 (not_6_out, n6);
  not not_7 (not_7_out, n7);
  not not_8 (not_8_out, n4);
  and E (E_out, not_8_out, n5, not_9_out, not_10_out);
  not not_9 (not_9_out, n6);
  not not_10 (not_10_out, n7);
  and OU (OU_out, n4, n5, not_11_out, not_12_out);
  not not_11 (not_11_out, n6);
  not not_12 (not_12_out, n7);
  not not_13 (not_13_out, n4);
  and NO (NO_out, not_13_out, n5, not_14_out, not_15_out);
  not not_14 (not_14_out, n6);
  not not_15 (not_15_out, n7);
  not not_16 (not_16_out, n5);
  and SHL (SHL_out, n4, not_16_out, n6, not_17_out);
  not not_17 (not_17_out, n7);
  not not_18 (not_18_out, n7);
  and SHR (SHR_out, n7, not_18_out, not_19_out, n7);
  not not_19 (not_19_out, n6);
  not not_20 (not_20_out, n7);
  and GTH (GTH_out, n7, not_20_out, not_21_out, not_22_out);
  not not_21 (not_21_out, n7);
  not not_22 (not_22_out, n7);
  not not_23 (not_23_out, n4);
  and EQU (EQU_out, not_23_out, n5, n6, not_24_out);
  not not_24 (not_24_out, n7);
  not not_25 (not_25_out, n5);
  and MV (MV_out, n4, not_25_out, n6, n7);
  not not_26 (not_26_out, n4);
  and READ (READ_out, not_26_out, n5, n6, n7);
  or or_1 (RegWrite, add_out, sub_out, E_out, OU_out, NO_out, SHL_out, SHR_out, GTH_out, EQU_out, MV_out, READ_out);
endmodule

module ALUSrcUC (
  input  n4,
  input  n5,
  input  n6,
  input  n7,
  output ALUSrc
);

  wire BEQ_out, BNE_out, EQU_out, GTH_out, MV_out, not_1_out, not_2_out, not_3_out, not_4_out, not_5_out,
       not_6_out, not_7_out, not_8_out, READ_out;

  not not_1 (not_1_out, n7);
  not not_2 (not_2_out, n4);
  not not_3 (not_3_out, n7);
  not not_4 (not_4_out, n5);
  not not_5 (not_5_out, n6);
  not not_6 (not_6_out, n5);
  not not_7 (not_7_out, n5);
  not not_8 (not_8_out, n4);
  and GTH (GTH_out, n4, n5, n6, not_1_out);
  and EQU (EQU_out, not_2_out, n5, n6, not_3_out);
  and MV (MV_out, n4, not_4_out, n6, n7);
  and BEQ (BEQ_out, n4, n5, not_5_out, n7);
  and BNE (BNE_out, not_6_out, not_7_out, n6, n7);
  and READ (READ_out, not_8_out, n5, n6, n7);
  or or_1 (ALUSrc, GTH_out, EQU_out, MV_out, BEQ_out, BNE_out, READ_out);
endmodule

module PCWriteUC (
  input  n4,
  input  n5,
  input  n6,
  input  n7,
  output PCWrite
);

  wire beq_out, bne_out, Jump_out, not_1_out, not_2_out, not_3_out, not_4_out, not_5_out;

  not not_1 (not_1_out, n4);
  not not_2 (not_2_out, n6);
  not not_3 (not_3_out, n6);
  not not_4 (not_4_out, n4);
  not not_5 (not_5_out, n5);
  and Jump (Jump_out, not_1_out, n5, not_2_out, n7);
  and beq (beq_out, n4, n5, not_3_out, n7);
  and bne (bne_out, not_4_out, not_5_out, n6, n7);
  or or_1 (PCWrite, Jump_out, beq_out, bne_out);
endmodule

module PCSrcUC (
  input  n4,
  input  n5,
  input  n6,
  input  n7,
  output PCSrc
);

  wire beq_out, bne_out, Jump_out, not_1_out, not_2_out, not_3_out, not_4_out, not_5_out;

  not not_1 (not_1_out, n4);
  not not_2 (not_2_out, n6);
  not not_3 (not_3_out, n6);
  not not_4 (not_4_out, n4);
  not not_5 (not_5_out, n5);
  and Jump (Jump_out, not_1_out, n5, not_2_out, n7);
  and beq (beq_out, n4, n5, not_3_out, n7);
  and bne (bne_out, not_4_out, not_5_out, n6, n7);
  or or_1 (PCSrc, Jump_out, beq_out, bne_out);
endmodule

module BranchUC (
  input  n4,
  input  n5,
  input  n6,
  input  n7,
  output Branch
);

  wire beq_out, bne_out, not_1_out, not_2_out, not_3_out;

  not not_1 (not_1_out, n6);
  not not_2 (not_2_out, n4);
  not not_3 (not_3_out, n5);
  and beq (beq_out, n4, n5, not_1_out, n7);
  and bne (bne_out, not_2_out, not_3_out, n6, n7);
  or or_1 (Branch, beq_out, bne_out);
endmodule

module ALUopUC (
  input  n4,
  input  n5,
  input  n6,
  input  n7,
  output [3:0] ALUOp
);

  wire E_out, EQU_out, GTH_out, MV_out, NO_out, not_1_out, not_2_out, not_3_out, not_4_out, not_5_out,
       not_6_out, not_7_out, not_8_out, not_9_out, not_10_out, not_11_out, not_12_out, not_13_out,
       not_14_out, not_15_out, not_16_out, not_17_out, not_18_out, not_19_out, not_20_out, not_21_out,
       not_22_out, not_23_out, not_24_out, not_25_out, not_26_out, not_27_out, not_28_out, OU_out, SHL_out,
       SHR_out, STH_out, sub_out;

  not not_1 (not_1_out, n5);
  not not_2 (not_2_out, n5);
  not not_3 (not_3_out, n6);
  not not_4 (not_4_out, n7);
  not not_5 (not_5_out, n5);
  not not_6 (not_6_out, n6);
  not not_7 (not_7_out, n7);
  not not_8 (not_8_out, n4);
  not not_9 (not_9_out, n6);
  not not_10 (not_10_out, n7);
  not not_11 (not_11_out, n6);
  not not_12 (not_12_out, n7);
  not not_13 (not_13_out, n4);
  not not_14 (not_14_out, n6);
  not not_15 (not_15_out, n7);
  not not_16 (not_16_out, n5);
  not not_17 (not_17_out, n7);
  not not_18 (not_18_out, n5);
  not not_19 (not_19_out, n6);
  not not_20 (not_20_out, n5);
  not not_21 (not_21_out, n6);
  not not_22 (not_22_out, n7);
  not not_23 (not_23_out, n4);
  not not_24 (not_24_out, n5);
  not not_25 (not_25_out, n6);
  not not_26 (not_26_out, n4);
  not not_27 (not_27_out, n7);
  not not_28 (not_28_out, n5);
  // AND_Gate add has open pins: in0=not_1_out, in1=not_2_out, in2=not_3_out, in3=not_4_out, out=open
  and sub (sub_out, n4, not_5_out, not_6_out, not_7_out);
  and E (E_out, not_8_out, n5, not_9_out, not_10_out);
  and OU (OU_out, n4, n5, not_11_out, not_12_out);
  and NO (NO_out, not_13_out, n5, not_14_out, not_15_out);
  and SHL (SHL_out, n4, not_16_out, n6, not_17_out);
  and SHR (SHR_out, n4, not_18_out, not_19_out, n7);
  and GTH (GTH_out, n4, not_20_out, not_21_out, not_22_out);
  and STH (STH_out, not_23_out, not_24_out, not_25_out, n7);
  and EQU (EQU_out, not_26_out, n5, n6, not_27_out);
  and MV (MV_out, n4, not_28_out, n6, n7);
  or or_1 (ALUOp[0], sub_out, OU_out, SHL_out, GTH_out, EQU_out);
  or or_2 (ALUOp[1], E_out, OU_out, SHR_out, GTH_out, MV_out);
  or or_3 (ALUOp[2], NO_out, SHL_out, SHR_out, GTH_out, MV_out);
  or or_4 (ALUOp[3], MV_out, EQU_out, STH_out);
endmodule

module MemToRegUC (
  input  n4,
  input  n5,
  input  n6,
  input  n7,
  output MemToReg
);

  wire not_1_out;

  not not_1 (not_1_out, n4);
  and and_1 (MemToReg, not_1_out, n5, n6, n7);
endmodule

module RegDstUC (
  input  n4,
  input  n5,
  input  n6,
  input  n7,
  input  [3:0] in_5,
  input  [3:0] in_6,
  input  [3:0] in_7,
  input  [3:0] in_8,
  output RegDstLogic
);

  wire comparator_1_eq, comparator_2_eq, comparator_3_eq, comparator_4_eq, or_1_out;

  Comparator #(.width(4)) comparator_1 (.a({n4, n5, n6, n7}), .b(in_5), .eq(comparator_1_eq));  // open: gt, lt
  Comparator #(.width(4)) comparator_2 (.a({n4, n5, n6, n7}), .b(in_6), .eq(comparator_2_eq));  // open: gt, lt
  Comparator #(.width(4)) comparator_3 (.a({n4, n5, n6, n7}), .b(in_7), .eq(comparator_3_eq));  // open: gt, lt
  Comparator #(.width(4)) comparator_4 (.a({n4, n5, n6, n7}), .b(in_8), .eq(comparator_4_eq));  // open: gt, lt
  or or_1 (or_1_out, comparator_1_eq, comparator_2_eq, comparator_3_eq, comparator_4_eq);
  not not_1 (RegDstLogic, or_1_out);

  // Notes on the sheet:
  //   cmp_jmp
  //   cmp_beq
  //   cmp_bne
  //   cmp_write
endmodule

module Main (
  input  RST,
  output [7:0] out_2
);

  wire alu_1_zero, ALUSrc, beq_out, bne_out, Branch, branch_out, CLK, Jump, MemRead, MemToReg, MemWrite,
       not_1_out, RegDstLogic, RegWrite;
  wire [1:0] multiplexer_3_out;
  wire [3:0] ALUOp, Opcode, rom_8b_1_rd;
  wire [7:0] adder_1_out, adder_2_out, alu_1_c, bit_extender_1_out, multiplexer_2_out, multiplexer_4_out,
       multiplexer_5_out, PC_q, ram_8b_1_dout, registers_1_rd_out, registers_1_rs_out;

  Multiplexer #(.width(8)) multiplexer_1 (.in0(multiplexer_2_out), .in1(bit_extender_1_out), .out(out_2), .sel(Jump));
  Register PC (.D(out_2), .en(1'b1), .clk(CLK), .Q(PC_q), .clr(RST));
  not not_1 (not_1_out, alu_1_zero);
  and bne (bne_out, Branch, not_1_out);
  and beq (beq_out, Branch, alu_1_zero);
  or u_branch (branch_out, bne_out, beq_out);
  Multiplexer #(.width(8)) multiplexer_2 (
    .in0(adder_1_out), .in1(adder_2_out), .out(multiplexer_2_out), .sel(branch_out));
  Adder adder_1 (.a(8'h1), .b(PC_q), .out(adder_1_out));  // open: cin, cout
  Adder adder_2 (.a(PC_q), .b(bit_extender_1_out), .out(adder_2_out));  // open: cin, cout
  ROM_8b rom_8b_1 (.PC(PC_q), .RD({Opcode, rom_8b_1_rd}), .RS({Opcode, rom_8b_1_rd}), .Op({Opcode, rom_8b_1_rd}));
  Clock u_CLK (.out(CLK));
  assign bit_extender_1_out = {{4{rom_8b_1_rd[3]}}, rom_8b_1_rd};  // Bit_Extender bit_extender_1
  Multiplexer #(.width(2)) multiplexer_3 (
    .in0(rom_8b_1_rd[3:2]), .in1(rom_8b_1_rd[1:0]), .out(multiplexer_3_out), .sel(RegDstLogic));
  Registers registers_1 (
    .WriteData(multiplexer_5_out), .RegWrite(RegWrite), .rd(rom_8b_1_rd[3:2]), .rs(rom_8b_1_rd[1:0]),
    .rW(multiplexer_3_out), .CLK(CLK), .RST(RST), .rd_out(registers_1_rd_out), .rs_out(registers_1_rs_out));  // open: WE
  Multiplexer #(.width(8)) multiplexer_4 (
    .in0(registers_1_rs_out), .in1(bit_extender_1_out), .out(multiplexer_4_out), .sel(ALUSrc));
  UC uc_1 (
    .Opcode(Opcode), .Jump(Jump), .MemRead(MemRead), .MemWrite(MemWrite), .MemToReg(MemToReg),
    .RegDstLogic(RegDstLogic), .ALUSrc(ALUSrc), .Branch(Branch), .ALUOp(ALUOp), .RegWrite(RegWrite));
  ALU alu_1 (.RD(registers_1_rd_out), .RS(multiplexer_4_out), .ALUOp(ALUOp), .C(alu_1_c), .Zero(alu_1_zero));
  Multiplexer #(.width(8)) multiplexer_5 (.in0(alu_1_c), .in1(ram_8b_1_dout), .out(multiplexer_5_out), .sel(MemToReg));
  RAM_8b ram_8b_1 (
    .A(alu_1_c), .MemWrite(MemWrite), .MemRead(MemRead), .Din(registers_1_rs_out), .CLK(CLK),
    .Dout(ram_8b_1_dout));
endmodule
